# Fritzing sketch fritzing diagram (saved by Fritzing 0.9.3b)
breadboards: 1

parts:
  Part1 = Arduino Uno (Rev3)
  M1 = DC Motor  # not connected
  M3 = DC Motor
  S1 = H-Bridge with L298N
  U4 = LIPO-1000mAh [package=lipo-1000]
  M5 = DC Motor
  M6 = DC Motor
  LED1 = LED - 5mm [color="Red (633nm)" package="5 mm [THT]"]
  LED2 = LED - 5mm [color="Green (570nm)" package="5 mm [THT]"]
  J1 = Piezo Speaker
  R1 = Resistor [tolerance=±5% resistance=220 package="0603 [SMD]"]
  R2 = Resistor [tolerance=±5% resistance=220 package="0603 [SMD]"]
  R3 = Resistor [tolerance=±5% resistance=220 package="0603 [SMD]"]
  M7 = fc-51 [package=THT]
  M8 = fc-51 [package=THT]
  M9 = fc-51 [package=THT]
  M10 = fc-51 [package=THT]

nets:
  N1: Part1.A0, M7.pin1
  N2: Part1.A1, M10.pin1
  N3: Part1.A2, M9.pin1
  N4: Part1.A3, M8.pin1
  N5: Part1.D9_PWM, S1.ENB
  N6: Part1.D10_PWM/SS, LED1.cathode
  N7: Part1.D11_PWM/MOSI, LED2.cathode
  N8: Part1.D12/MISO, J1.pin2
  N9: Part1.D3_PWM, S1.ENA
  N10: Part1.D4, S1.IN4
  N11: Part1.D5_PWM, S1.IN3
  N12: Part1.D6_PWM, S1.IN2
  N13: Part1.D7, S1.IN1
  N14: Part1.5V, M7.pin3, M8.pin3, M9.pin3, M10.pin3
  GND: Part1.GND, S1.GND, U4.-, R1.Pin_0, R2.Pin_0, R3.Pin_0, M7.pin2, M8.pin2, M9.pin2, M10.pin2
  VIN: Part1.VIN, S1.5V
  N15: M3.pin_1, S1.M1-01, M6.pin_1
  N16: M3.pin_2, S1.M1-02, M6.pin_2
  N17: S1.12V, U4.+
  N18: S1.M2-01, M5.pin_2
  N19: S1.M2-02, M5.pin_1
  N20: LED1.anode, R1.Pin_1
  N21: LED2.anode, R2.Pin_1
  N22: J1.pin1, R3.Pin_1

custom parts:
  H-Bridge with L298N: h-bridge
